// Logisim project rho beta.circ as structural Verilog: 1 circuit, main circuit main
module main (
);

  wire _0_out, _1_out, _2_out, _3_out, _4_out, _5_out, _6_out, _7_out, _8_out, _9_out, and_1_out, and_2_out,
       and_3_out, and_4_out, and_5_out, and_6_out, and_7_out, and_8_out, d_ff_1_qn, d_ff_2_qn,
       multiplexer_1_out, not_1_out, not_2_out, not_3_out, not_4_out, not_5_out, not_6_out, not_7_out,
       not_8_out, not_9_out, not_10_out, not_11_out, not_12_out, not_13_out, not_14_out, not_15_out,
       not_16_out, not_17_out, not_18_out, not_19_out, not_20_out, not_21_out, not_22_out, not_23_out,
       not_24_out, not_25_out, not_26_out, not_27_out, not_28_out, not_29_out, not_30_out, not_31_out,
       not_32_out, not_33_out, not_34_out, not_35_out, not_36_out, or_1_out, or_2_out;
  wire [1:0] d_ff_2_q;

  Button _0 (.out(_0_out));
  Button _1 (.out(_1_out));
  Button _2 (.out(_2_out));
  Button _4 (.out(_4_out));
  Button _3 (.out(_3_out));
  Button _6 (.out(_6_out));
  Button _5 (.out(_5_out));
  Button _8 (.out(_8_out));
  Button _7 (.out(_7_out));
  Button _9 (.out(_9_out));
  not not_1 (not_1_out, _0_out);
  not not_2 (not_2_out, _1_out);
  not not_3 (not_3_out, _2_out);
  not not_4 (not_4_out, _3_out);
  and and_1 (and_1_out, not_1_out, not_2_out, not_3_out, not_4_out, _4_out, not_5_out, not_6_out, not_7_out, not_8_out, not_9_out);
  not not_5 (not_5_out, _5_out);
  not not_6 (not_6_out, _6_out);
  not not_7 (not_7_out, _7_out);
  not not_8 (not_8_out, _8_out);
  not not_9 (not_9_out, _9_out);
  not not_10 (not_10_out, _0_out);
  not not_11 (not_11_out, _1_out);
  not not_12 (not_12_out, _3_out);
  not not_13 (not_13_out, _4_out);
  and and_2 (and_2_out, not_10_out, not_11_out, _2_out, not_12_out, not_13_out, not_14_out, not_15_out, not_16_out, not_17_out, not_18_out);
  not not_14 (not_14_out, _5_out);
  not not_15 (not_15_out, _6_out);
  not not_16 (not_16_out, _7_out);
  not not_17 (not_17_out, _8_out);
  not not_18 (not_18_out, _9_out);
  not not_19 (not_19_out, _0_out);
  not not_20 (not_20_out, _1_out);
  not not_21 (not_21_out, _2_out);
  not not_22 (not_22_out, _3_out);
  not not_23 (not_23_out, _4_out);
  and and_3 (and_3_out, not_19_out, not_20_out, not_21_out, not_22_out, not_23_out, not_24_out, _6_out, not_25_out, not_26_out, not_27_out);
  not not_24 (not_24_out, _5_out);
  not not_25 (not_25_out, _7_out);
  not not_26 (not_26_out, _8_out);
  not not_27 (not_27_out, _9_out);
  not not_28 (not_28_out, _0_out);
  not not_29 (not_29_out, _1_out);
  not not_30 (not_30_out, _2_out);
  not not_31 (not_31_out, _3_out);
  not not_32 (not_32_out, _4_out);
  and and_4 (and_4_out, not_28_out, not_29_out, not_30_out, not_31_out, not_32_out, not_33_out, not_34_out, not_35_out, not_36_out, _9_out);
  not not_33 (not_33_out, _5_out);
  not not_34 (not_34_out, _6_out);
  not not_35 (not_35_out, _7_out);
  not not_36 (not_36_out, _8_out);
  or or_1 (or_1_out, _0_out, _1_out, _2_out, _3_out, _4_out, _5_out, _6_out, _7_out, _8_out, _9_out);
  Multiplexer #(.select(2), .enable("false")) multiplexer_1 (
    .in0(and_1_out), .in1(and_2_out), .in2(and_3_out), .in3(and_4_out), .out(multiplexer_1_out),
    .sel(d_ff_2_q));
  LED Unlocked (.in(and_5_out));
  and and_5 (and_5_out, multiplexer_1_out, d_ff_2_q[0], d_ff_2_q[1]);
  D_Flip_Flop #(.trigger("falling")) d_ff_1 (
    .clk(or_1_out), .D(or_2_out), .Q(d_ff_2_q[1]), .Qn(d_ff_1_qn));  // open: preset, en, reset
  or or_2 (or_2_out, and_7_out, and_6_out);
  and and_6 (and_6_out, d_ff_1_qn, d_ff_2_q[0], multiplexer_1_out);
  and and_7 (and_7_out, multiplexer_1_out, d_ff_2_q[1], d_ff_2_qn);
  and and_8 (and_8_out, multiplexer_1_out, d_ff_2_qn);
  D_Flip_Flop #(.trigger("falling")) d_ff_2 (
    .clk(or_1_out), .D(and_8_out), .Q(d_ff_2_q[0]), .Qn(d_ff_2_qn));  // open: preset, en, reset
endmodule
